# Fritzing sketch Bluetooth (saved by Fritzing 0.9.2b)
breadboards: 1

parts:
  元件1 = Arduino Nano (Rev3.0)
  元件2 = Bluetooth Mate Silver

nets:
  N1: 元件1.D10, 元件2.TX_5V
  N2: 元件1.D11/MOSI, 元件2.RX_5V
  GND: 元件1.GND, 元件2.GND
  5V: 元件1.5V, 元件2.VCC
